// Logisim project do_not_touch_unless_a_TA_tells_you_to.circ as structural Verilog: 1 circuit, main circuit TL1 ALU
module TL1_ALU (
  input  [7:0] A,
  input  [7:0] B,
  input  [1:0] Selector,
  output [7:0] Output
);


  // Other names for the same wires on the sheet: SEL[1:0] = Selector
endmodule
