// Logisim project BOB-2200.circ as structural Verilog: 4 circuits, main circuit Datapath
module Datapath (
  output [3:0] out_1,
  output [31:0] Bus,
  output [31:0] PC_Value,
  output [3:0] out_4
);

  wire ALUHi, ALULo, ChkCmp, Clock, CmpOut, comparator_1_eq, comparator_1_lt, CondType, DrALU, DrCmp, DrMEM,
       DrOFF, DrPC, DrREG, LdA, LdB, LdCmp, LdIR, LdMAR, LdPC, not_1_out, OPTest, Reset, WrMEM, WrREG;
  wire [1:0] RegSel;
  wire [23:0] MAR_q;
  wire [27:0] IR;
  wire [31:0] A_q, alu_1_out_4, B_q, bit_extender_1_out, bit_extender_2_out, ram_1_data, registers_1_data_out;

  Clock clock_1 (.out(Clock));
  LED led_1 (.in(DrALU));
  LED led_2 (.in(DrPC));
  LED led_3 (.in(WrMEM));
  LED led_4 (.in(WrREG));
  Button button_1 (.out(Reset));
  Register #(.width(32)) PC (.D(Bus), .en(LdPC), .Q(PC_Value), .clk(Clock), .clr(Reset));
  Comparator #(.width(32)) comparator_1 (
    .a(Bus), .b({32{1'b0}}), .eq(comparator_1_eq), .lt(comparator_1_lt));  // open: gt
  not not_1 (not_1_out, comparator_1_eq);
  LED led_5 (.in(DrMEM));
  LED led_6 (.in(DrREG));
  LED led_7 (.in(RegSel[0]));
  assign Bus = DrPC ? PC_Value : 32'bz;  // Controlled_Buffer controlled_buffer_1
  Multiplexer #(.disabled(0), .enable("false")) multiplexer_1 (
    .in0(not_1_out), .in1(comparator_1_lt), .out(CmpOut), .sel(CondType));
  LED led_8 (.in(DrOFF));
  LED led_9 (.in(RegSel[1]));
  Register #(.width(32)) A (.D(Bus), .en(LdA), .Q(A_q), .clk(Clock), .clr(Reset));
  ALU alu_1 (.in_1(A_q), .in_2(B_q), .in_3({ALUHi, ALULo}), .out_4(alu_1_out_4));
  assign Bus = DrALU ? alu_1_out_4 : 32'bz;  // Controlled_Buffer controlled_buffer_2
  LED led_10 (.in(LdPC));
  LED led_11 (.in(DrCmp));
  LED led_12 (.in(ALULo));
  LED led_13 (.in(ALUHi));
  Register #(.width(32)) B (.D(Bus), .en(LdB), .Q(B_q), .clk(Clock), .clr(Reset));
  assign Bus = DrCmp ? bit_extender_1_out : 32'bz;  // Controlled_Buffer controlled_buffer_3
  assign bit_extender_1_out = {{31{CmpOut}}, CmpOut};  // Bit_Extender bit_extender_1
  LED led_14 (.in(LdB));
  LED led_15 (.in(LdA));
  LED led_16 (.in(OPTest));
  LED led_17 (.in(LdMAR));
  LED led_18 (.in(LdIR));
  LED led_19 (.in(DrCmp));
  LED led_20 (.in(ChkCmp));
  Registers registers_1 (
    .in_1(Bus), .in_2(Clock), .in_3(WrREG), .in_4(Reset), .in_5(out_4), .Data_Out(registers_1_data_out));
  LED led_21 (.in(LdCmp));
  LED led_22 (.in(CondType));
  assign Bus = DrREG ? registers_1_data_out : 32'bz;  // Controlled_Buffer controlled_buffer_4
  Register #(.width(24)) MAR (.D(Bus[23:0]), .en(LdMAR), .Q(MAR_q), .clk(Clock), .clr(Reset));
  MicroController microcontroller_1 (
    .in_1(out_1), .in_2(Clock), .in_3(Reset), .in_4(CmpOut), .out_5(DrREG), .out_6(DrMEM), .out_7(DrALU),
    .out_8(DrPC), .out_9(DrOFF), .out_10(LdPC), .out_11(LdIR), .out_12(LdMAR), .out_13(LdA), .out_14(LdB),
    .out_15(LdCmp), .out_16(WrREG), .out_17(WrMEM), .out_18(RegSel[0]), .out_19(RegSel[1]), .out_20(ALULo),
    .out_21(ALUHi), .out_22(OPTest), .out_23(ChkCmp), .out_24(DrCmp), .out_25(CondType));
  Multiplexer #(.select(2), .width(4), .disabled(0), .enable("false")) multiplexer_2 (
    .in0(IR[27:24]), .in1(IR[23:20]), .in2(IR[3:0]), .out(out_4), .sel(RegSel));  // open: in3
  RAM #(.addrWidth(24), .dataWidth(32), .bus("separate")) ram_1 (
    .addr(MAR_q), .din(Bus), .data(ram_1_data), .str(WrMEM), .clk(Clock));  // open: sel, ld, clr
  assign Bus = DrMEM ? ram_1_data : 32'bz;  // Controlled_Buffer controlled_buffer_5
  Register #(.width(32)) u_IR (.D(Bus), .en(LdIR), .Q({out_1, IR}), .clk(Clock), .clr(Reset));
  assign bit_extender_2_out = {{12{IR[19]}}, IR[19:0]};  // Bit_Extender bit_extender_2
  assign Bus = DrOFF ? bit_extender_2_out : 32'bz;  // Controlled_Buffer controlled_buffer_6

  // Other names for the same wires on the sheet: func[1:0] = {ALUHi, ALULo}; OFF[19:0] = IR[19:0]; Rz[3:0] = IR[3:0];
  //   Ry[3:0] = IR[23:20]; Rx[3:0] = IR[27:24]; IR[31:28] = out_1; OP[3:0] = out_1; regno[3:0] = out_4;
  //   RegSelLo = RegSel[0]; RegSelHi = RegSel[1]
endmodule

module ALU (
  input  [31:0] in_1,
  input  [31:0] in_2,
  input  [1:0] in_3,
  output [31:0] out_4
);

  wire [31:0] Out_1, Out_2, Out_3, Out_4_t;

  Adder #(.width(32)) adder_1 (.a(in_1), .b(in_2), .out(Out_1), .cin(1'b0));  // open: cout
  Subtractor #(.width(32)) subtractor_1 (.a(in_1), .b(in_2), .out(Out_2), .bin(1'b0));  // open: bout
  assign Out_3 = ~(in_1 & in_2);  // NAND_Gate nand_1, 32 bits wide
  Adder #(.width(32)) adder_2 (.a(in_1), .b(32'h1), .out(Out_4_t), .cin(1'b0));  // open: cout
  Multiplexer #(.select(2), .width(32), .disabled(0), .enable("false")) multiplexer_1 (
    .in0(Out_1), .in1(Out_2), .in2(Out_3), .in3(Out_4_t), .out(out_4), .sel(in_3));

  // Other names for the same wires on the sheet: A[31:0] = in_1; B[31:0] = in_2; Func[1:0] = in_3; Out[31:0] = out_4

  // Notes on the sheet:
  //   A+B = Out 1
  //   00: ADD
  //   01: SUB
  //   10: NAND
  //   11: A+1
  //   A-B = Out 2
  //   NAND A&B
  //   A+1 = Out 4
endmodule

module MicroController (
  input  [3:0] in_1,
  input  in_2,
  input  in_3,
  input  in_4,
  output out_5,
  output out_6,
  output out_7,
  output out_8,
  output out_9,
  output out_10,
  output out_11,
  output out_12,
  output out_13,
  output out_14,
  output out_15,
  output out_16,
  output out_17,
  output out_18,
  output out_19,
  output out_20,
  output out_21,
  output out_22,
  output out_23,
  output out_24,
  output out_25
);

  wire [5:0] multiplexer_1_out, Next_State, rom_1_data, rom_2_data, State_Register_q;
  wire [31:27] rom_3_data;

  ROM #(.addrWidth(4), .dataWidth(6)) rom_1 (.addr(in_1), .data(rom_1_data));  // open: sel
  ROM #(.addrWidth(2), .dataWidth(6)) rom_2 (.addr({1'b0, in_4}), .data(rom_2_data));  // open: sel
  Multiplexer #(.select(2), .width(6), .disabled(0), .enable("false")) multiplexer_1 (
    .in0(Next_State), .in1(rom_1_data), .in2(rom_2_data), .out(multiplexer_1_out), .sel({out_23, out_22}));  // open: in3
  Register #(.width(6)) State_Register (
    .D(multiplexer_1_out), .Q(State_Register_q), .clk(in_2), .clr(in_3));  // open: en
  ROM #(.addrWidth(6), .dataWidth(32)) rom_3 (
    .addr(State_Register_q),
    .data({rom_3_data, out_25, out_24, out_23, out_22, out_21, out_20, out_19, out_18, out_17, out_16, out_15, out_14, out_13, out_12, out_11, out_10, out_9, out_8, out_7, out_6, out_5, Next_State}));  // open: sel

  // Other names for the same wires on the sheet: CmpOut = in_4; DrREG = out_5; DrMEM = out_6; DrALU = out_7;
  //   DrPC = out_8; DrOFF = out_9; LdPC = out_10; LdIR = out_11; LdMAR = out_12; LdA = out_13; LdB = out_14;
  //   LdCmp = out_15; WrREG = out_16; WrMEM = out_17; RegSelLo = out_18; RegSelHi = out_19; ALULo = out_20;
  //   ALUHi = out_21; OPTest = out_22; ChkCmp = out_23; DrCmp = out_24; CondType = out_25; Clock = in_2;
  //   OP[3:0] = in_1; Reset = in_3

  // Notes on the sheet:
  //   Sequencer ROM
  //   Condition ROM
  //   contents of rom_1 (hex, n*v repeats v):
  //   3 6 9 c 10 14 1a 1c 1d 21
  //   contents of rom_2 (hex, n*v repeats v):
  //   0 17
  //   Main ROM
  //   contents of rom_3 (hex, n*v repeats v):
  //   6201 1082 e00900 84044 108045 20100 84047 108048 220100 8404a 840b 20100 8404d 840e 210f 20080 84051
  //   8412 2113 40040 4055 88056 1200100 4218 8419 900 2021b 80840 1c 8405e 10805f 5200120 2020000 4222
  //   8423 20100
endmodule

module Registers (
  input  [31:0] in_1,
  input  in_2,
  input  in_3,
  input  in_4,
  input  [3:0] in_5,
  output [31:0] Data_Out
);

  wire and_1_out, and_2_out, and_3_out, and_4_out, and_5_out, and_6_out, and_7_out, and_8_out, and_9_out,
       and_10_out, and_11_out, and_12_out, and_13_out, and_14_out, and_15_out, and_16_out, decoder_1_out0,
       decoder_1_out1, decoder_1_out2, decoder_1_out3, decoder_1_out4, decoder_1_out5, decoder_1_out6,
       decoder_1_out7, decoder_1_out8, decoder_1_out9, decoder_1_out10, decoder_1_out11, decoder_1_out12,
       decoder_1_out13, decoder_1_out14, decoder_1_out15;
  wire [31:0] a0, a1, a2, at, fp, k0, ra, s0, s1, s2, sp, t0, t1, t2, v0, zero;

  and and_1 (and_1_out, decoder_1_out0, in_3);
  and and_2 (and_2_out, decoder_1_out1, in_3);
  and and_3 (and_3_out, decoder_1_out2, in_3);
  and and_4 (and_4_out, decoder_1_out3, in_3);
  and and_5 (and_5_out, decoder_1_out4, in_3);
  and and_6 (and_6_out, decoder_1_out5, in_3);
  and and_7 (and_7_out, decoder_1_out6, in_3);
  and and_8 (and_8_out, decoder_1_out7, in_3);
  Register #(.width(32)) u_zero (.D(in_1), .en(and_1_out), .Q(zero), .clk(in_2), .clr(1'b1));
  Register #(.width(32)) u_at (.D(in_1), .en(and_2_out), .Q(at), .clk(in_2), .clr(in_4));
  Register #(.width(32)) u_v0 (.D(in_1), .en(and_3_out), .Q(v0), .clk(in_2), .clr(in_4));
  Register #(.width(32)) u_a0 (.D(in_1), .en(and_4_out), .Q(a0), .clk(in_2), .clr(in_4));
  Register #(.width(32)) u_a1 (.D(in_1), .en(and_5_out), .Q(a1), .clk(in_2), .clr(in_4));
  Register #(.width(32)) u_a2 (.D(in_1), .en(and_6_out), .Q(a2), .clk(in_2), .clr(in_4));
  Register #(.width(32)) u_t0 (.D(in_1), .en(and_7_out), .Q(t0), .clk(in_2), .clr(in_4));
  Register #(.width(32)) u_t1 (.D(in_1), .en(and_8_out), .Q(t1), .clk(in_2), .clr(in_4));
  Decoder #(.select(4), .enable("false")) decoder_1 (
    .out0(decoder_1_out0), .out1(decoder_1_out1), .out2(decoder_1_out2), .out3(decoder_1_out3),
    .out4(decoder_1_out4), .out5(decoder_1_out5), .out6(decoder_1_out6), .out7(decoder_1_out7),
    .out8(decoder_1_out8), .out9(decoder_1_out9), .out10(decoder_1_out10), .out11(decoder_1_out11),
    .out12(decoder_1_out12), .out13(decoder_1_out13), .out14(decoder_1_out14), .out15(decoder_1_out15),
    .sel(in_5));
  and and_9 (and_9_out, decoder_1_out8, in_3);
  and and_10 (and_10_out, decoder_1_out9, in_3);
  and and_11 (and_11_out, decoder_1_out10, in_3);
  and and_12 (and_12_out, decoder_1_out11, in_3);
  and and_13 (and_13_out, decoder_1_out12, in_3);
  and and_14 (and_14_out, decoder_1_out13, in_3);
  and and_15 (and_15_out, decoder_1_out14, in_3);
  and and_16 (and_16_out, decoder_1_out15, in_3);
  Register #(.width(32)) u_t2 (.D(in_1), .en(and_9_out), .Q(t2), .clk(in_2), .clr(in_4));
  Register #(.width(32)) u_s0 (.D(in_1), .en(and_10_out), .Q(s0), .clk(in_2), .clr(in_4));
  Register #(.width(32)) u_s1 (.D(in_1), .en(and_11_out), .Q(s1), .clk(in_2), .clr(in_4));
  Register #(.width(32)) u_s2 (.D(in_1), .en(and_12_out), .Q(s2), .clk(in_2), .clr(in_4));
  Register #(.width(32)) u_k0 (.D(in_1), .en(and_13_out), .Q(k0), .clk(in_2), .clr(in_4));
  Register #(.width(32)) u_sp (.D(in_1), .en(and_14_out), .Q(sp), .clk(in_2), .clr(in_4));
  Register #(.width(32)) u_fp (.D(in_1), .en(and_15_out), .Q(fp), .clk(in_2), .clr(in_4));
  Register #(.width(32)) u_ra (.D(in_1), .en(and_16_out), .Q(ra), .clk(in_2), .clr(in_4));
  Multiplexer #(.select(4), .width(32), .disabled(0), .enable("false")) multiplexer_1 (
    .in0(zero), .in1(at), .in2(v0), .in3(a0), .in4(a1), .in5(a2), .in6(t0), .in7(t1), .in8(t2), .in9(s0),
    .in10(s1), .in11(s2), .in12(k0), .in13(sp), .in14(fp), .in15(ra), .out(Data_Out), .sel(in_5));

  // Other names for the same wires on the sheet: Clock = in_2; Data_In[31:0] = in_1; regno[3:0] = in_5; Reset = in_4;
  //   WrREG = in_3
endmodule
