// Logisim project BOB-2200a.circ as structural Verilog: 5 circuits, main circuit my circuit
module my_circuit (
);

  wire CLK, Clr, cmpOut, comparator_1_eq, comparator_1_gt, comparison_logic_1_output, DrALU, DrIO, EnInt, IE,
       Int, IntAck, ldA, ldB, ldCmp, LdIR, ldMAR, LdPC, OnInt, or_1_out;
  wire [0:0] inters;
  wire [1:0] comp, func;
  wire [3:0] OpCode, others, regno, Rx, Ry, Rz;
  wire [4:0] drives;
  wire [19:4] IR_q;
  wire [31:0] A_q, alu_1_out_4, B_q, bit_extender_1_out, bit_extender_2_out, controlled_buffer_1_out, MAR_q,
       multiplexer_1_out, PC_q, ram_1_data, register_file_1_out, timer_device_1_p5;

  Clock clock_1 (.out(CLK));
  Register #(.width(32)) PC (.D(controlled_buffer_1_out), .en(LdPC), .Q(PC_q), .clk(CLK), .clr(Clr));
  Comparator #(.width(32)) comparator_1 (
    .a(PC_q), .b({32{1'b0}}), .gt(comparator_1_gt), .eq(comparator_1_eq));  // open: lt
  or or_1 (or_1_out, comparator_1_gt, comparator_1_eq);
  Button button_1 (.out(Clr));
  Multiplexer #(.width(32), .disabled(0), .enable("false")) multiplexer_1 (
    .in0({32{1'b0}}), .in1(PC_q), .out(multiplexer_1_out), .sel(or_1_out));
  assign controlled_buffer_1_out = drives[3] ? multiplexer_1_out : 32'bz;  // Controlled_Buffer controlled_buffer_1
  Comparison_Logic comparison_logic_1 (
    .\input (controlled_buffer_1_out), .mode(comp[1]), .\output (comparison_logic_1_output));
  Microcontroller microcontroller_1 (
    .opcode(OpCode), .CmpOut(cmpOut), .CLK(CLK), .Drives({drives[4:3], DrALU, drives[1:0]}),
    .Loads({ldCmp, ldB, ldA, ldMAR, LdIR, LdPC}), .Others({func, others}), .Comp(comp), .OnInt(OnInt),
    .Inter({DrIO, IntAck, EnInt, inters[0]}), .Clr(Clr));
  Register #(.width(32)) A (.D(controlled_buffer_1_out), .en(ldA), .Q(A_q), .clk(CLK), .clr(Clr));
  // Probe on func
  ALU alu_1 (.A(A_q), .B(B_q), .Select(func), .out_4(alu_1_out_4));
  assign controlled_buffer_1_out = DrALU ? alu_1_out_4 : 32'bz;  // Controlled_Buffer controlled_buffer_2
  Register #(.width(1)) register_1 (.D(comparison_logic_1_output), .en(ldCmp), .Q(cmpOut), .clk(CLK), .clr(Clr));
  and and_1 (OnInt, IE, Int);
  Register #(.width(32)) B (.D(controlled_buffer_1_out), .en(ldB), .Q(B_q), .clk(CLK), .clr(Clr));
  assign bit_extender_1_out = {{31{1'b0}}, cmpOut};  // Bit_Extender bit_extender_1
  assign controlled_buffer_1_out = comp[0] ? bit_extender_1_out : 32'bz;  // Controlled_Buffer controlled_buffer_3
  Register_File register_file_1 (
    .WtReg(others[0]), .IN(controlled_buffer_1_out), .regno(regno), .clk(CLK), .clr(Clr),
    .OUT(register_file_1_out));
  assign controlled_buffer_1_out = drives[0] ? register_file_1_out : 32'bz;  // Controlled_Buffer controlled_buffer_4
  Register #(.width(1)) u_IE (.D(EnInt), .en(inters[0]), .Q(IE), .clk(CLK), .clr(Clr));
  Register #(.width(32)) MAR (.D(controlled_buffer_1_out), .en(ldMAR), .Q(MAR_q), .clk(CLK), .clr(Clr));
  Multiplexer #(.select(2), .width(4), .disabled(0), .enable("false")) multiplexer_2 (
    .in0(Rx), .in1(Ry), .in2(Rz), .in3(4'b1100), .out(regno), .sel(others[3:2]));
  RAM #(.addrWidth(24), .dataWidth(32), .bus("separate")) ram_1 (
    .addr(MAR_q[23:0]), .din(controlled_buffer_1_out), .data(ram_1_data), .str(others[1]), .clk(CLK),
    .ld(1'b1));  // open: sel, clr
  assign controlled_buffer_1_out = drives[1] ? ram_1_data : 32'bz;  // Controlled_Buffer controlled_buffer_5
  assign controlled_buffer_1_out = DrIO ? timer_device_1_p5 : 32'bz;  // Controlled_Buffer controlled_buffer_6
  Pull_Resistor pull_resistor_1 (.node(Int));
  // Timer_Device timer_device_1: pin names not known; wires that end beside it: IntAck, CLK, Int, 32'h3e8, timer_device_1_p5, 32'h1
  Register #(.width(32)) IR (
    .D(controlled_buffer_1_out), .en(LdIR), .Q({OpCode, Rx, Ry, IR_q, Rz}), .clk(CLK), .clr(Clr));
  assign bit_extender_2_out = {{12{IR_q[19]}}, {IR_q, Rz}};  // Bit_Extender bit_extender_2
  assign controlled_buffer_1_out = drives[4] ? bit_extender_2_out : 32'bz;  // Controlled_Buffer controlled_buffer_7
  // Probe on controlled_buffer_1_out

  // Other names for the same wires on the sheet: DrCmp = comp[0]; CondType = comp[1]; DrREG = drives[0];
  //   DrMEM = drives[1]; drives[2] = DrALU; DrPC = drives[3]; DrOFF = drives[4]; LdEnInt = inters[0];
  //   inters[3:1] = {DrIO, IntAck, EnInt}; loads[5:0] = {ldCmp, ldB, ldA, ldMAR, LdIR, LdPC}; WrREG = others[0];
  //   WrMEM = others[1]; RegSel[1:0] = others[3:2]; others[5:4] = func

  // Notes on the sheet:
  //   Register File
  //   Main Memory
  //   INT Line
endmodule

module ALU (
  input  [31:0] A,
  input  [31:0] B,
  input  [1:0] Select,
  output [31:0] out_4
);

  wire [31:0] adder_1_out, adder_2_out, nand_1_out, subtractor_1_out;

  Adder #(.width(32)) adder_1 (.a(A), .b(B), .out(adder_1_out));  // open: cin, cout
  Subtractor #(.width(32)) subtractor_1 (.a(A), .b(B), .out(subtractor_1_out));  // open: bin, bout
  assign nand_1_out = ~(A & B);  // NAND_Gate nand_1, 32 bits wide
  Adder #(.width(32)) adder_2 (.a(A), .b({32{1'b0}}), .out(adder_2_out), .cin(1'b1));  // open: cout
  // Probe on adder_1_out
  // Probe on subtractor_1_out
  // Probe on nand_1_out
  Multiplexer #(.select(2), .width(32), .disabled(0), .enable("false")) multiplexer_1 (
    .in0(adder_1_out), .in1(subtractor_1_out), .in2(nand_1_out), .in3(adder_2_out), .out(out_4), .sel(Select));

  // Other names for the same wires on the sheet: Output[31:0] = out_4
endmodule

module Comparison_Logic (
  input  [31:0] \input ,
  input  mode,
  output \output 
);

  wire comparator_1_eq, comparator_1_lt, not_1_out;

  Comparator #(.width(32)) comparator_1 (
    .a(\input ), .b({32{1'b0}}), .eq(comparator_1_eq), .lt(comparator_1_lt));  // open: gt
  Multiplexer #(.disabled(0), .enable("false")) multiplexer_1 (
    .in0(not_1_out), .in1(comparator_1_lt), .out(\output ), .sel(mode));
  not not_1 (not_1_out, comparator_1_eq);
  Pull_Resistor pull_resistor_1 (.node(\output ));
endmodule

module Microcontroller (
  input  CLK,
  input  Clr,
  input  [3:0] opcode,
  input  CmpOut,
  input  OnInt,
  output [4:0] Drives,
  output [5:0] Loads,
  output [5:0] Others,
  output [1:0] Comp,
  output [3:0] Inter
);

  wire [1:0] rom_1_data_2;
  wire [5:0] cmpROM, intROM, multiplexer_1_out, opROM, register_1_q, rom_1_data;

  // Probe on rom_1_data_2
  Multiplexer #(.select(2), .width(6), .disabled(0), .enable("false")) multiplexer_1 (
    .in0(rom_1_data), .in1(opROM), .in2(cmpROM), .in3(intROM), .out(multiplexer_1_out), .sel(rom_1_data_2));
  Register #(.width(6)) register_1 (.D(multiplexer_1_out), .Q(register_1_q), .clk(CLK), .clr(Clr));  // open: en
  ROM #(.addrWidth(6), .dataWidth(31)) rom_1 (
    .addr(register_1_q), .data({Inter, Comp, rom_1_data_2, Others, Loads, Drives, rom_1_data}));  // open: sel
  ROM #(.addrWidth(4), .dataWidth(6)) rom_2 (.addr(opcode), .data(opROM));  // open: sel
  ROM #(.addrWidth(2), .dataWidth(6)) rom_3 (.addr({1'b0, CmpOut}), .data(cmpROM));  // open: sel
  ROM #(.addrWidth(2), .dataWidth(6)) rom_4 (.addr({1'b0, OnInt}), .data(intROM));  // open: sel

  // Notes on the sheet:
  //   Main Rom
  //   Sequencer Rom
  //   Comparison Rom
  //   Interrupt ROM
  //   contents of rom_1 (hex, n*v repeats v):
  //   1800000 6202 10a8 84044 108045 20100 84047 108048 420100 440a 8804b 20100 440d 8804e 210f 20080 4411
  //   88052 2113 40040 4055 88056 210117 100003f 4219 841a 900 2021c 80840 1d 8405f 108060 4210121 2020000
  //   4223 8424 20100 18000000 8000000 180865 e00900 81a022a 6000202b 880
  //   contents of rom_2 (hex, n*v repeats v):
  //   3 6 9 c 10 14 1b 1d 1e 22 25 26 27
  //   contents of rom_3 (hex, n*v repeats v):
  //   0 18
  //   contents of rom_4 (hex, n*v repeats v):
  //   1 29
endmodule

module Register_File (
  input  WtReg,
  input  [31:0] IN,
  input  clk,
  input  clr,
  input  [3:0] regno,
  output [31:0] OUT
);

  wire Wt0, Wt1, Wt2, Wt3, Wt4, Wt5, Wt6, Wt7, Wt8, Wt9, Wt10, Wt11, Wt12, Wt13, Wt14, Wt15;
  wire [31:0] Reg0, Reg1, Reg2, Reg3, Reg4, Reg5, Reg6, Reg7, Reg8, Reg9, Reg10, Reg11, Reg12, Reg13, Reg14,
       Reg15;

  Demultiplexer #(.select(4), .disabled(0), .enable("false")) demultiplexer_1 (
    .out0(Wt0), .out1(Wt1), .out2(Wt2), .out3(Wt3), .out4(Wt4), .out5(Wt5), .out6(Wt6), .out7(Wt7),
    .out8(Wt8), .out9(Wt9), .out10(Wt10), .out11(Wt11), .out12(Wt12), .out13(Wt13), .out14(Wt14),
    .out15(Wt15), .in(WtReg), .sel(regno));
  Register #(.width(32)) zero (.D(IN), .en(Wt0), .Q(Reg0), .clk(clk), .clr(1'b1));
  Register #(.width(32)) t2 (.D(IN), .en(Wt8), .Q(Reg8), .clk(clk), .clr(clr));
  Register #(.width(32)) at (.D(IN), .en(Wt1), .Q(Reg1), .clk(clk), .clr(clr));
  Register #(.width(32)) s0 (.D(IN), .en(Wt9), .Q(Reg9), .clk(clk), .clr(clr));
  Register #(.width(32)) v0 (.D(IN), .en(Wt2), .Q(Reg2), .clk(clk), .clr(clr));
  Register #(.width(32)) s1 (.D(IN), .en(Wt10), .Q(Reg10), .clk(clk), .clr(clr));
  Register #(.width(32)) a0 (.D(IN), .en(Wt3), .Q(Reg3), .clk(clk), .clr(clr));
  Register #(.width(32)) s2 (.D(IN), .en(Wt11), .Q(Reg11), .clk(clk), .clr(clr));
  Register #(.width(32)) a1 (.D(IN), .en(Wt4), .Q(Reg4), .clk(clk), .clr(clr));
  Register #(.width(32)) k0 (.D(IN), .en(Wt12), .Q(Reg12), .clk(clk), .clr(clr));
  Register #(.width(32)) a2 (.D(IN), .en(Wt5), .Q(Reg5), .clk(clk), .clr(clr));
  Register #(.width(32)) sp (.D(IN), .en(Wt13), .Q(Reg13), .clk(clk), .clr(clr));
  Multiplexer #(.select(4), .width(32), .disabled(0), .enable("false")) multiplexer_1 (
    .in0(Reg0), .in1(Reg1), .in2(Reg2), .in3(Reg3), .in4(Reg4), .in5(Reg5), .in6(Reg6), .in7(Reg7),
    .in8(Reg8), .in9(Reg9), .in10(Reg10), .in11(Reg11), .in12(Reg12), .in13(Reg13), .in14(Reg14),
    .in15(Reg15), .out(OUT), .sel(regno));
  Register #(.width(32)) t0 (.D(IN), .en(Wt6), .Q(Reg6), .clk(clk), .clr(clr));
  Register #(.width(32)) fp (.D(IN), .en(Wt14), .Q(Reg14), .clk(clk), .clr(clr));
  Register #(.width(32)) t1 (.D(IN), .en(Wt7), .Q(Reg7), .clk(clk), .clr(clr));
  Register #(.width(32)) ra (.D(IN), .en(Wt15), .Q(Reg15), .clk(clk), .clr(clr));

  // Other names for the same wires on the sheet: DATA[31:0] = IN
endmodule
