// Logisim project BOB2200-pipeline.circ as structural Verilog: 9 circuits, main circuit main
module main (
);

  wire ALUSel1, ALUSel2, and_3_out, Branch, BSel, Clk, Clr, comparator_1_eq, comparator_2_eq,
       comparator_2_lt, CompType, ex_mem_buffer_1_comp_result_2, Flush, HaltPC, mem_wb_buffer_1_compres_2,
       not_1_out, not_2_out, or_1_out, or_2_out, or_3_out, PCSel, RegSel, Stall, WR, WrEN, WrMEM;
  wire [1:0] func, WBSel;
  wire [3:0] ex_mem_buffer_1_opcode_2, ex_mem_buffer_1_rx_2, idrr_ex_buffer_1_opcode_2,
       idrr_ex_buffer_1_rx_2, if_idrr_buffer_1_opcode, if_idrr_buffer_1_rx, if_idrr_buffer_1_ry,
       if_idrr_buffer_1_rz, mem_wb_buffer_1_rx_2, multiplexer_3_out, multiplexer_4_out, multiplexer_5_out;
  wire [11:0] idrr_ex_buffer_1_consig_2;
  wire [12:0] control_1_signals, ex_mem_buffer_1_consig_2, multiplexer_6_out;
  wire [12:3] mem_wb_buffer_1_consig_2;
  wire [19:0] if_idrr_buffer_1_offset;
  wire [31:0] adder_1_out, adder_2_out, alu_1_output, bit_extender_1_out, bit_extender_2_out,
       dual_ported_register_file_1_out1, dual_ported_register_file_1_out2, ex_mem_buffer_1_alu_result_2,
       ex_mem_buffer_1_data2_2, ex_mem_buffer_1_pc_2, idrr_ex_buffer_1_out_1_2, idrr_ex_buffer_1_out_2_2,
       idrr_ex_buffer_1_pc_2, idrr_ex_buffer_1_signext_2, if_idrr_buffer_1_pc_2,
       mem_wb_buffer_1_alu_result_2, mem_wb_buffer_1_data_2, mem_wb_buffer_1_pc_2, multiplexer_1_out,
       multiplexer_2_out, multiplexer_7_out, multiplexer_8_out, multiplexer_9_out, multiplexer_11_out, PC_q,
       ram_1_data, ram_2_data;

  or or_1 (or_1_out, Flush, and_3_out);
  and and_1 (Flush, PCSel, Branch);
  Clock clock_1 (.out(Clk));
  Button button_1 (.out(Clr));
  Multiplexer #(.width(32), .disabled(0), .enable("false")) multiplexer_1 (
    .in0(adder_1_out), .in1(multiplexer_9_out), .out(multiplexer_1_out), .sel(or_1_out));
  and and_2 (WR, not_1_out, HaltPC);
  not not_1 (not_1_out, Stall);
  Multiplexer #(.width(32), .disabled(0), .enable("false")) multiplexer_2 (
    .in0(PC_q), .in1(multiplexer_1_out), .out(multiplexer_2_out), .sel(WR));
  Register #(.width(32)) PC (.D(multiplexer_2_out), .en(1'b1), .Q(PC_q), .clk(Clk), .clr(Clr));
  and and_3 (and_3_out, PCSel, comparator_1_eq);
  Comparator #(.width(4)) comparator_1 (
    .a(4'b0110), .b(idrr_ex_buffer_1_opcode_2), .eq(comparator_1_eq));  // open: gt, lt
  Adder #(.width(32)) adder_1 (.a(32'h1), .b(PC_q), .out(adder_1_out));  // open: cin, cout
  RAM #(.addrWidth(24), .dataWidth(32)) ram_1 (.addr(PC_q[23:0]), .data(ram_1_data), .clk(Clk));  // open: sel, ld, clr
  IF_IDRR_Buffer if_idrr_buffer_1 (
    .PC(adder_1_out), .Instruction(ram_1_data), .in_1(WR), .in_2(Clk), .in_3(or_2_out),
    .PC_2(if_idrr_buffer_1_pc_2), .OpCode(if_idrr_buffer_1_opcode), .Rx(if_idrr_buffer_1_rx),
    .Ry(if_idrr_buffer_1_ry), .Rz(if_idrr_buffer_1_rz), .Offset(if_idrr_buffer_1_offset));
  or or_2 (or_2_out, Clr, Flush);
  Multiplexer #(.width(4), .disabled(0), .enable("false")) multiplexer_3 (
    .in0(if_idrr_buffer_1_rx), .in1(if_idrr_buffer_1_rz), .out(multiplexer_3_out), .sel(RegSel));
  Control control_1 (
    .OpCode(if_idrr_buffer_1_opcode), .in_1(Clk), .in_2(Clr),
    .Signals({control_1_signals[12], HaltPC, RegSel, control_1_signals[9:0]}));
  Multiplexer #(.width(4), .disabled(0), .enable("false")) multiplexer_4 (
    .in0(if_idrr_buffer_1_opcode), .in1(4'b0000), .out(multiplexer_4_out), .sel(Stall));
  Multiplexer #(.width(4), .disabled(0), .enable("false")) multiplexer_5 (
    .in0(if_idrr_buffer_1_rx), .in1(4'b0000), .out(multiplexer_5_out), .sel(Stall));
  assign bit_extender_1_out = {{12{if_idrr_buffer_1_offset[19]}}, if_idrr_buffer_1_offset};  // Bit_Extender bit_extender_1
  Stall_Unit stall_unit_1 (
    .ID_Ry(if_idrr_buffer_1_ry), .ID_Rz(if_idrr_buffer_1_rz), .EX_Rx(idrr_ex_buffer_1_rx_2),
    .MEM_Rx(ex_mem_buffer_1_rx_2), .WB_Rx(mem_wb_buffer_1_rx_2), .Stall(Stall));
  Dual_Ported_Register_File dual_ported_register_file_1 (
    .CLK(Clk), .WrREGNO(mem_wb_buffer_1_rx_2), .RdREGNO1(if_idrr_buffer_1_ry), .RdREGNO2(multiplexer_3_out),
    .INPUT(multiplexer_11_out), .OUT1(dual_ported_register_file_1_out1),
    .OUT2(dual_ported_register_file_1_out2), .WrEN(WrEN));
  Multiplexer #(.width(13), .disabled(0), .enable("false")) multiplexer_6 (
    .in0({control_1_signals[12], HaltPC, RegSel, control_1_signals[9:0]}), .in1(13'hc84),
    .out(multiplexer_6_out), .sel(Stall));
  IDRR_EX_Buffer idrr_ex_buffer_1 (
    .ConSig(multiplexer_6_out), .PC(if_idrr_buffer_1_pc_2), .Out_1(dual_ported_register_file_1_out1),
    .Out_2(dual_ported_register_file_1_out2), .SignExt(bit_extender_1_out), .Rx(multiplexer_5_out),
    .OpCode(multiplexer_4_out), .in_1(Clk), .in_2(or_3_out),
    .ConSig_2({PCSel, idrr_ex_buffer_1_consig_2[11:10], func, ALUSel1, ALUSel2, BSel, CompType, idrr_ex_buffer_1_consig_2[3:0]}),
    .PC_2(idrr_ex_buffer_1_pc_2), .Out_1_2(idrr_ex_buffer_1_out_1_2), .Out_2_2(idrr_ex_buffer_1_out_2_2),
    .SignExt_2(idrr_ex_buffer_1_signext_2), .Rx_2(idrr_ex_buffer_1_rx_2), .OpCode_2(idrr_ex_buffer_1_opcode_2));
  or or_3 (or_3_out, Clr, Flush);
  Adder #(.width(32)) adder_2 (
    .a(idrr_ex_buffer_1_pc_2), .b(idrr_ex_buffer_1_signext_2), .out(adder_2_out));  // open: cin, cout
  Multiplexer #(.width(32), .disabled(0), .enable("false")) multiplexer_7 (
    .in0(idrr_ex_buffer_1_pc_2), .in1(idrr_ex_buffer_1_out_1_2), .out(multiplexer_7_out), .sel(ALUSel1));
  Multiplexer #(.width(32), .disabled(0), .enable("false")) multiplexer_8 (
    .in0(idrr_ex_buffer_1_out_2_2), .in1(idrr_ex_buffer_1_signext_2), .out(multiplexer_8_out), .sel(ALUSel2));
  ALU alu_1 (.A(multiplexer_7_out), .B(multiplexer_8_out), .func(func), .Output(alu_1_output));
  Comparator #(.width(32)) comparator_2 (
    .a(alu_1_output), .b({32{1'b0}}), .eq(comparator_2_eq), .lt(comparator_2_lt));  // open: gt
  not not_2 (not_2_out, comparator_2_eq);
  Multiplexer #(.width(32), .disabled(0), .enable("false")) multiplexer_9 (
    .in0(adder_2_out), .in1(multiplexer_7_out), .out(multiplexer_9_out), .sel(BSel));
  Pull_Resistor pull_resistor_1 (.node(Branch));
  Multiplexer #(.disabled(0), .enable("false")) multiplexer_10 (
    .in0(not_2_out), .in1(comparator_2_lt), .out(Branch), .sel(CompType));
  EX_MEM_Buffer ex_mem_buffer_1 (
    .PC_Sext(multiplexer_9_out),
    .ConSig({PCSel, idrr_ex_buffer_1_consig_2[11:10], func, ALUSel1, ALUSel2, BSel, CompType, idrr_ex_buffer_1_consig_2[3:0]}),
    .ALU_Result(alu_1_output), .Data2(idrr_ex_buffer_1_out_2_2), .Comp_Result(Branch),
    .Rx(idrr_ex_buffer_1_rx_2), .OpCode(idrr_ex_buffer_1_opcode_2), .PC(idrr_ex_buffer_1_pc_2), .in_1(Clk),
    .in_2(Clr), .ConSig_2({ex_mem_buffer_1_consig_2[12:4], WrMEM, ex_mem_buffer_1_consig_2[2:0]}),
    .ALU_Result_2(ex_mem_buffer_1_alu_result_2), .Data2_2(ex_mem_buffer_1_data2_2),
    .Comp_Result_2(ex_mem_buffer_1_comp_result_2), .Rx_2(ex_mem_buffer_1_rx_2),
    .OpCode_2(ex_mem_buffer_1_opcode_2), .PC_2(ex_mem_buffer_1_pc_2));  // open: PC_Sext_2
  RAM #(.addrWidth(24), .dataWidth(32), .bus("separate")) ram_2 (
    .addr(ex_mem_buffer_1_alu_result_2[23:0]), .din(ex_mem_buffer_1_data2_2), .data(ram_2_data), .str(WrMEM),
    .clk(Clk));  // open: sel, ld, clr
  Pull_Resistor pull_resistor_2 (.node(WrEN));
  MEM_WB_Buffer mem_wb_buffer_1 (
    .ConSig({ex_mem_buffer_1_consig_2[12:4], WrMEM, ex_mem_buffer_1_consig_2[2:0]}),
    .PC(ex_mem_buffer_1_pc_2), .Data(ram_2_data), .ALU_Result(ex_mem_buffer_1_alu_result_2),
    .Rx(ex_mem_buffer_1_rx_2), .OpCode(ex_mem_buffer_1_opcode_2), .CompRes(ex_mem_buffer_1_comp_result_2),
    .in_1(Clk), .in_2(Clr), .ConSig_2({mem_wb_buffer_1_consig_2, WrEN, WBSel}), .PC_2(mem_wb_buffer_1_pc_2),
    .Data_2(mem_wb_buffer_1_data_2), .ALU_Result_2(mem_wb_buffer_1_alu_result_2),
    .Rx_2(mem_wb_buffer_1_rx_2), .CompRes_2(mem_wb_buffer_1_compres_2));  // open: OpCode_2
  Multiplexer #(.select(2), .width(32), .disabled(0), .enable("false")) multiplexer_11 (
    .in0(mem_wb_buffer_1_alu_result_2), .in1(mem_wb_buffer_1_data_2), .in2(mem_wb_buffer_1_pc_2),
    .in3(bit_extender_2_out), .out(multiplexer_11_out), .sel(WBSel));
  assign bit_extender_2_out = {{31{1'b0}}, mem_wb_buffer_1_compres_2};  // Bit_Extender bit_extender_2

  // Notes on the sheet:
  //   OP
  //   RX
endmodule

module Dual_Ported_Register_File (
  input  CLK,
  input  WrEN,
  input  [3:0] WrREGNO,
  input  [3:0] RdREGNO1,
  input  [3:0] RdREGNO2,
  input  [31:0] INPUT,
  output [31:0] OUT1,
  output [31:0] OUT2
);

  wire En_a0, En_a1, En_a2, En_at, En_fp, En_k0, En_ra, En_s0, En_s1, En_s2, En_sp, En_t0, En_t1, En_t2,
       En_v0;
  wire [31:0] a0, a1, a2, at, fp, k0, ra, s0, s1, s2, sp, t0, t1, t2, v0, zero;

  Decoder #(.select(4), .disabled(0)) decoder_1 (
    .out1(En_at), .out2(En_v0), .out3(En_a0), .out4(En_a1), .out5(En_a2), .out6(En_t0), .out7(En_t1),
    .out8(En_t2), .out9(En_s0), .out10(En_s1), .out11(En_s2), .out12(En_k0), .out13(En_sp), .out14(En_fp),
    .out15(En_ra), .sel(WrREGNO), .en(WrEN));  // open: out0
  Register #(.width(32)) u_zero (.D(INPUT), .en(1'b0), .Q(zero), .clk(CLK));  // open: clr
  Register #(.width(32)) u_at (.D(INPUT), .en(En_at), .Q(at), .clk(CLK));  // open: clr
  Register #(.width(32)) u_v0 (.D(INPUT), .en(En_v0), .Q(v0), .clk(CLK));  // open: clr
  Register #(.width(32)) u_a0 (.D(INPUT), .en(En_a0), .Q(a0), .clk(CLK));  // open: clr
  Register #(.width(32)) u_a1 (.D(INPUT), .en(En_a1), .Q(a1), .clk(CLK));  // open: clr
  Register #(.width(32)) u_a2 (.D(INPUT), .en(En_a2), .Q(a2), .clk(CLK));  // open: clr
  Register #(.width(32)) u_t0 (.D(INPUT), .en(En_t0), .Q(t0), .clk(CLK));  // open: clr
  Register #(.width(32)) u_t1 (.D(INPUT), .en(En_t1), .Q(t1), .clk(CLK));  // open: clr
  Multiplexer #(.select(4), .width(32), .disabled(0), .enable("false")) multiplexer_1 (
    .in0(zero), .in1(at), .in2(v0), .in3(a0), .in4(a1), .in5(a2), .in6(t0), .in7(t1), .in8(t2), .in9(s0),
    .in10(s1), .in11(s2), .in12(k0), .in13(sp), .in14(fp), .in15(ra), .out(OUT2), .sel(RdREGNO2));
  Register #(.width(32)) u_t2 (.D(INPUT), .en(En_t2), .Q(t2), .clk(CLK));  // open: clr
  Register #(.width(32)) u_s0 (.D(INPUT), .en(En_s0), .Q(s0), .clk(CLK));  // open: clr
  Register #(.width(32)) u_s1 (.D(INPUT), .en(En_s1), .Q(s1), .clk(CLK));  // open: clr
  Register #(.width(32)) u_s2 (.D(INPUT), .en(En_s2), .Q(s2), .clk(CLK));  // open: clr
  Register #(.width(32)) u_k0 (.D(INPUT), .en(En_k0), .Q(k0), .clk(CLK));  // open: clr
  Register #(.width(32)) u_sp (.D(INPUT), .en(En_sp), .Q(sp), .clk(CLK));  // open: clr
  Register #(.width(32)) u_fp (.D(INPUT), .en(En_fp), .Q(fp), .clk(CLK));  // open: clr
  Register #(.width(32)) u_ra (.D(INPUT), .en(En_ra), .Q(ra), .clk(CLK));  // open: clr
  Multiplexer #(.select(4), .width(32), .disabled(0), .enable("false")) multiplexer_2 (
    .in0(zero), .in1(at), .in2(v0), .in3(a0), .in4(a1), .in5(a2), .in6(t0), .in7(t1), .in8(t2), .in9(s0),
    .in10(s1), .in11(s2), .in12(k0), .in13(sp), .in14(fp), .in15(ra), .out(OUT1), .sel(RdREGNO1));

  // Notes on the sheet:
  //   MODIFY AT YOUR OWN RISK
endmodule

// FBUF
module IF_IDRR_Buffer (
  input  in_1,
  input  in_2,
  input  in_3,
  input  [31:0] PC,
  input  [31:0] Instruction,
  output [31:0] PC_2,
  output [3:0] OpCode,
  output [3:0] Rx,
  output [3:0] Ry,
  output [3:0] Rz,
  output [19:0] Offset
);

  Register #(.width(32)) register_1 (.D(PC), .en(in_1), .Q(PC_2), .clk(in_2), .clr(in_3));
  Register #(.width(32)) register_2 (.D(Instruction), .en(in_1), .Q({OpCode, Rx, Ry, Offset}), .clk(in_2), .clr(in_3));

  assign Rz = Offset[3:0];

  // Other names for the same wires on the sheet: Clk = in_2; Clr = in_3; WR = in_1
endmodule

// DBUF
module IDRR_EX_Buffer (
  input  in_1,
  input  in_2,
  input  [12:0] ConSig,
  input  [31:0] PC,
  input  [31:0] Out_1,
  input  [31:0] Out_2,
  input  [31:0] SignExt,
  input  [3:0] Rx,
  input  [3:0] OpCode,
  output [12:0] ConSig_2,
  output [31:0] PC_2,
  output [31:0] Out_1_2,
  output [31:0] Out_2_2,
  output [31:0] SignExt_2,
  output [3:0] Rx_2,
  output [3:0] OpCode_2
);

  Register #(.width(13)) register_1 (.D(ConSig), .en(1'b1), .Q(ConSig_2), .clk(in_1), .clr(in_2));
  Register #(.width(32)) register_2 (.D(PC), .en(1'b1), .Q(PC_2), .clk(in_1), .clr(in_2));
  Register #(.width(32)) register_3 (.D(Out_1), .en(1'b1), .Q(Out_1_2), .clk(in_1), .clr(in_2));
  Register #(.width(32)) register_4 (.D(Out_2), .en(1'b1), .Q(Out_2_2), .clk(in_1), .clr(in_2));
  Register #(.width(32)) register_5 (.D(SignExt), .en(1'b1), .Q(SignExt_2), .clk(in_1), .clr(in_2));
  Register #(.width(4)) register_6 (.D(Rx), .en(1'b1), .Q(Rx_2), .clk(in_1), .clr(in_2));
  Register #(.width(4)) register_7 (.D(OpCode), .en(1'b1), .Q(OpCode_2), .clk(in_1), .clr(in_2));

  // Other names for the same wires on the sheet: Clk = in_1; Clr = in_2
endmodule

// EBUF
module EX_MEM_Buffer (
  input  in_1,
  input  in_2,
  input  [31:0] PC_Sext,
  input  [12:0] ConSig,
  input  [31:0] ALU_Result,
  input  [31:0] Data2,
  input  Comp_Result,
  input  [3:0] Rx,
  input  [3:0] OpCode,
  input  [31:0] PC,
  output [31:0] PC_Sext_2,
  output [12:0] ConSig_2,
  output [31:0] ALU_Result_2,
  output [31:0] Data2_2,
  output Comp_Result_2,
  output [3:0] Rx_2,
  output [3:0] OpCode_2,
  output [31:0] PC_2
);

  Register #(.width(32)) register_1 (.D(PC_Sext), .en(1'b1), .Q(PC_Sext_2), .clk(in_1), .clr(in_2));
  Register #(.width(13)) register_2 (.D(ConSig), .en(1'b1), .Q(ConSig_2), .clk(in_1), .clr(in_2));
  Register #(.width(32)) register_3 (.D(ALU_Result), .en(1'b1), .Q(ALU_Result_2), .clk(in_1), .clr(in_2));
  Register #(.width(32)) u_Data2 (.D(Data2), .en(1'b1), .Q(Data2_2), .clk(in_1), .clr(in_2));
  Register #(.width(1)) register_4 (.D(Comp_Result), .en(1'b1), .Q(Comp_Result_2), .clk(in_1), .clr(in_2));
  Register #(.width(4)) register_5 (.D(Rx), .en(1'b1), .Q(Rx_2), .clk(in_1), .clr(in_2));
  Register #(.width(4)) u_OpCode (.D(OpCode), .en(1'b1), .Q(OpCode_2), .clk(in_1), .clr(in_2));
  Register #(.width(32)) register_6 (.D(PC), .en(1'b1), .Q(PC_2), .clk(in_1), .clr(in_2));

  // Other names for the same wires on the sheet: Clk = in_1; Clr = in_2
endmodule

// MBUF
module MEM_WB_Buffer (
  input  in_1,
  input  in_2,
  input  [12:0] ConSig,
  input  [31:0] PC,
  input  [31:0] Data,
  input  [31:0] ALU_Result,
  input  [3:0] Rx,
  input  [3:0] OpCode,
  input  CompRes,
  output [12:0] ConSig_2,
  output [31:0] PC_2,
  output [31:0] Data_2,
  output [31:0] ALU_Result_2,
  output [3:0] Rx_2,
  output [3:0] OpCode_2,
  output CompRes_2
);

  Register #(.width(13)) register_1 (.D(ConSig), .en(1'b1), .Q(ConSig_2), .clk(in_1), .clr(in_2));
  Register #(.width(32)) register_2 (.D(PC), .en(1'b1), .Q(PC_2), .clk(in_1), .clr(in_2));
  Register #(.width(32)) register_3 (.D(Data), .en(1'b1), .Q(Data_2), .clk(in_1), .clr(in_2));
  Register #(.width(32)) u_ALU_Result (.D(ALU_Result), .en(1'b1), .Q(ALU_Result_2), .clk(in_1), .clr(in_2));
  Register #(.width(4)) register_4 (.D(Rx), .en(1'b1), .Q(Rx_2), .clk(in_1), .clr(in_2));
  Register #(.width(4)) u_OpCode (.D(OpCode), .en(1'b1), .Q(OpCode_2), .clk(in_1), .clr(in_2));
  Register #(.width(1)) u_CompRes (.D(CompRes), .en(1'b1), .Q(CompRes_2), .clk(in_1), .clr(in_2));

  // Other names for the same wires on the sheet: Clk = in_1; Clr = in_2
endmodule

module ALU (
  input  [31:0] A,
  input  [31:0] B,
  input  [1:0] func,
  output [31:0] Output
);

  wire [31:0] adder_1_out, adder_2_out, nand_1_out, subtractor_1_out;

  Adder #(.width(32)) adder_1 (.a(A), .b(B), .out(adder_1_out));  // open: cin, cout
  assign nand_1_out = ~(A & B);  // NAND_Gate nand_1, 32 bits wide
  Subtractor #(.width(32)) subtractor_1 (.a(A), .b(B), .out(subtractor_1_out));  // open: bin, bout
  Adder #(.width(32)) adder_2 (.a(A), .b({32{1'b0}}), .out(adder_2_out), .cin(1'b1));  // open: cout
  Multiplexer #(.select(2), .width(32), .disabled(0), .enable("false")) multiplexer_1 (
    .in0(adder_1_out), .in1(nand_1_out), .in2(subtractor_1_out), .in3(adder_2_out), .out(Output), .sel(func));
endmodule

module Control (
  input  in_1,
  input  in_2,
  input  [3:0] OpCode,
  output [12:0] Signals
);

  ROM #(.addrWidth(4), .dataWidth(13)) rom_1 (.addr(OpCode), .data(Signals));  // open: sel

  // Other names for the same wires on the sheet: Clk = in_1; Clr = in_2

  // Notes on the sheet:
  //   contents of rom_1 (hex, n*v repeats v):
  //   c84 d84 cc4 cc5 8c8 1a80 18a6 0 e97 844
endmodule

// Stall
module Stall_Unit (
  input  [3:0] ID_Ry,
  input  [3:0] ID_Rz,
  input  [3:0] EX_Rx,
  input  [3:0] MEM_Rx,
  input  [3:0] WB_Rx,
  output Stall
);

  wire and_1_out, and_2_out, comparator_1_eq, comparator_2_eq, comparator_3_eq, comparator_4_eq,
       comparator_5_eq, comparator_6_eq, comparator_7_eq, comparator_8_eq, not_1_out, not_2_out, or_1_out,
       or_2_out;

  Comparator #(.width(4), .mode("unsigned")) comparator_1 (.a(ID_Ry), .b(EX_Rx), .eq(comparator_1_eq));  // open: gt, lt
  Comparator #(.width(4), .mode("unsigned")) comparator_2 (
    .a(ID_Ry), .b(MEM_Rx), .eq(comparator_2_eq));  // open: gt, lt
  Comparator #(.width(4), .mode("unsigned")) comparator_3 (.a(ID_Ry), .b(WB_Rx), .eq(comparator_3_eq));  // open: gt, lt
  Comparator #(.width(4), .mode("unsigned")) comparator_4 (.a(ID_Rz), .b(EX_Rx), .eq(comparator_4_eq));  // open: gt, lt
  Comparator #(.width(4), .mode("unsigned")) comparator_5 (
    .a(ID_Rz), .b(MEM_Rx), .eq(comparator_5_eq));  // open: gt, lt
  Comparator #(.width(4), .mode("unsigned")) comparator_6 (.a(ID_Rz), .b(WB_Rx), .eq(comparator_6_eq));  // open: gt, lt
  Comparator #(.width(4), .mode("unsigned")) comparator_7 (
    .a(ID_Ry), .b(4'b0000), .eq(comparator_7_eq));  // open: gt, lt
  or or_1 (or_1_out, comparator_4_eq, comparator_5_eq, comparator_6_eq);
  Comparator #(.width(4), .mode("unsigned")) comparator_8 (
    .a(ID_Rz), .b(4'b0000), .eq(comparator_8_eq));  // open: gt, lt
  not not_1 (not_1_out, comparator_7_eq);
  or or_2 (or_2_out, comparator_1_eq, comparator_2_eq, comparator_3_eq);
  not not_2 (not_2_out, comparator_8_eq);
  and and_1 (and_1_out, not_1_out, or_2_out);
  and and_2 (and_2_out, or_1_out, not_2_out);
  or or_3 (Stall, and_1_out, and_2_out);
endmodule
